// Logisim project Gates.circ as structural Verilog: 6 circuits, main circuit nand
module \nand  (
  input  a,
  input  b,
  output out
);

  nand nand_1 (out, a, b);
endmodule

module \not  (
  input  in,
  output out
);

  \nand  nand_1 (.a(in), .b(in), .out(out));
endmodule

module \and  (
  input  a,
  input  b,
  output out
);

  wire nand_1_out;

  \nand  nand_1 (.a(a), .b(b), .out(nand_1_out));
  \not  not_1 (.in(nand_1_out), .out(out));
endmodule

module And16 (
  input  [15:0] a,
  input  [15:0] b,
  output [15:0] out
);

  \and  and_1 (.a(a[0]), .b(b[0]), .out(out[0]));
  \and  and_2 (.a(a[1]), .b(b[1]), .out(out[1]));
  \and  and_3 (.a(a[2]), .b(b[2]), .out(out[2]));
  \and  and_4 (.a(a[3]), .b(b[3]), .out(out[3]));
  \and  and_5 (.a(a[4]), .b(b[4]), .out(out[4]));
  \and  and_6 (.a(a[5]), .b(b[5]), .out(out[5]));
  \and  and_7 (.a(a[6]), .b(b[6]), .out(out[6]));
  \and  and_8 (.a(a[7]), .b(b[7]), .out(out[7]));
  \and  and_9 (.a(a[8]), .b(b[8]), .out(out[8]));
  \and  and_10 (.a(a[9]), .b(b[9]), .out(out[9]));
  \and  and_11 (.a(a[10]), .b(b[10]), .out(out[10]));
  \and  and_12 (.a(a[11]), .b(b[11]), .out(out[11]));
  \and  and_13 (.a(a[12]), .b(b[12]), .out(out[12]));
  \and  and_14 (.a(a[13]), .b(b[13]), .out(out[13]));
  \and  and_15 (.a(a[14]), .b(b[14]), .out(out[14]));
  \and  and_16 (.a(a[15]), .b(b[15]), .out(out[15]));
endmodule

module Or (
  input  a,
  input  b,
  output out
);

  wire not_1_out, not_2_out;

  \not  not_1 (.in(a), .out(not_1_out));
  \not  not_2 (.in(b), .out(not_2_out));
  \nand  nand_1 (.a(not_1_out), .b(not_2_out), .out(out));
endmodule

module Xor (
  input  a,
  input  b,
  output out
);

  wire and_1_out, and_2_out, not_1_out, not_2_out;

  \not  not_1 (.in(a), .out(not_1_out));
  \not  not_2 (.in(b), .out(not_2_out));
  \and  and_1 (.a(not_2_out), .b(a), .out(and_1_out));
  Or or_1 (.a(and_1_out), .b(and_2_out), .out(out));
  \and  and_2 (.a(not_1_out), .b(b), .out(and_2_out));
endmodule
