// Logisim project Main.circ as structural Verilog
module Mux (
  input  a,
  input  b,
  input  sel,
  output Out
);

  wire and_1_out, and_2_out, not_1_out;

  not not_1 (not_1_out, sel);
  and and_1 (and_1_out, not_1_out, a);
  and and_2 (and_2_out, b, sel);
  or or_1 (Out, and_1_out, and_2_out);
endmodule

module DMux (
  input  in,
  input  sel,
  output b,
  output a
);

  wire not_1_out;

  and and_1 (b, in, sel);
  not not_1 (not_1_out, sel);
  and and_2 (a, in, not_1_out);
endmodule

module Mux16 (
  input  [15:0] a,
  input  [15:0] b,
  input  Sel,
  output [15:0] out_4
);

  Mux mux_1 (.a(a[14]), .b(b[14]), .Out(out_4[14]), .sel(Sel));
  Mux mux_2 (.a(a[15]), .b(b[15]), .Out(out_4[15]), .sel(Sel));
  Mux mux_3 (.a(a[13]), .b(b[13]), .Out(out_4[13]), .sel(Sel));
  Mux mux_4 (.a(a[12]), .b(b[12]), .Out(out_4[12]), .sel(Sel));
  Mux mux_5 (.a(a[11]), .b(b[11]), .Out(out_4[11]), .sel(Sel));
  Mux mux_6 (.a(a[10]), .b(b[10]), .Out(out_4[10]), .sel(Sel));
  Mux mux_7 (.a(a[9]), .b(b[9]), .Out(out_4[9]), .sel(Sel));
  Mux mux_8 (.a(a[8]), .b(b[8]), .Out(out_4[8]), .sel(Sel));
  Mux mux_9 (.a(a[7]), .b(b[7]), .Out(out_4[7]), .sel(Sel));
  Mux mux_10 (.a(a[6]), .b(b[6]), .Out(out_4[6]), .sel(Sel));
  Mux mux_11 (.a(a[5]), .b(b[5]), .Out(out_4[5]), .sel(Sel));
  Mux mux_12 (.a(a[4]), .b(b[4]), .Out(out_4[4]), .sel(Sel));
  Mux mux_13 (.a(a[3]), .b(b[3]), .Out(out_4[3]), .sel(Sel));
  Mux mux_14 (.a(a[2]), .b(b[2]), .Out(out_4[2]), .sel(Sel));
  Mux mux_15 (.a(a[1]), .b(b[1]), .Out(out_4[1]), .sel(Sel));
  Mux mux_16 (.a(a[0]), .b(b[0]), .Out(out_4[0]), .sel(Sel));
endmodule

module Main (
  input  in_1,
  input  in_2,
  input  [15:0] in_3,
  input  [15:0] in_4,
  input  in_5,
  input  in_6,
  input  in_7,
  input  in_8,
  output [15:0] out_9,
  output out_10,
  output out_11
);

  ALU alu_1 (
    .x(in_3), .zx(in_1), .nx(in_2), .y(in_4), .f(in_7), .zy(in_5), .ny(in_6), .no(in_8), .out(out_9),
    .ng(out_10), .zr(out_11));
endmodule

module Mux4Way16 (
  input  [15:0] a,
  input  [15:0] b,
  input  [15:0] c,
  input  [15:0] d,
  input  [1:0] Sel,
  output [15:0] Out
);

  wire [15:0] mux16_1_out_4, mux16_2_out_4;

  Mux16 mux16_1 (.a(a), .b(b), .out_4(mux16_1_out_4), .Sel(Sel[0]));
  Mux16 mux16_2 (.a(c), .b(d), .out_4(mux16_2_out_4), .Sel(Sel[0]));
  Mux16 mux16_3 (.a(mux16_1_out_4), .b(mux16_2_out_4), .out_4(Out), .Sel(Sel[1]));
endmodule

module Mux8Way16 (
  input  [15:0] a,
  input  [15:0] b,
  input  [15:0] c,
  input  [15:0] d,
  input  [15:0] e,
  input  [15:0] f,
  input  [15:0] g,
  input  [15:0] h,
  input  [2:0] Sel,
  output [15:0] out
);

  wire [15:0] mux4way16_1_out, mux4way16_2_out;

  Mux4Way16 mux4way16_1 (.a(a), .b(b), .c(c), .d(d), .Out(mux4way16_1_out), .Sel(Sel[1:0]));
  Mux4Way16 mux4way16_2 (.a(e), .b(f), .c(g), .d(h), .Out(mux4way16_2_out), .Sel(Sel[1:0]));
  Mux16 mux16_1 (.a(mux4way16_1_out), .b(mux4way16_2_out), .out_4(out), .Sel(Sel[2]));
endmodule

module HalfAdder (
  input  a,
  input  b,
  output Sum,
  output Carry
);

  xor xor_1 (Sum, a, b);
  and and_1 (Carry, a, b);
endmodule

module FullAdder (
  input  a,
  input  b,
  input  c,
  output Carry,
  output Sum
);

  wire halfadder_1_carry, halfadder_1_sum, halfadder_2_carry;

  HalfAdder halfadder_1 (.a(a), .b(b), .Sum(halfadder_1_sum), .Carry(halfadder_1_carry));
  or or_1 (Carry, halfadder_1_carry, halfadder_2_carry);
  HalfAdder halfadder_2 (.a(halfadder_1_sum), .b(c), .Sum(Sum), .Carry(halfadder_2_carry));
endmodule

module Add16 (
  input  [15:0] a,
  input  [15:0] b,
  output [15:0] out
);

  wire fulladder_1_carry, fulladder_2_carry, fulladder_3_carry, fulladder_4_carry, fulladder_5_carry,
       fulladder_6_carry, fulladder_7_carry, fulladder_8_carry, fulladder_9_carry, fulladder_10_carry,
       fulladder_11_carry, fulladder_12_carry, fulladder_13_carry, fulladder_14_carry, halfadder_1_carry;

  HalfAdder halfadder_1 (.a(a[0]), .b(b[0]), .Sum(out[0]), .Carry(halfadder_1_carry));
  FullAdder fulladder_1 (.a(a[1]), .b(b[1]), .c(halfadder_1_carry), .Carry(fulladder_1_carry), .Sum(out[1]));
  FullAdder fulladder_2 (.a(a[2]), .b(b[2]), .c(fulladder_1_carry), .Carry(fulladder_2_carry), .Sum(out[2]));
  FullAdder fulladder_3 (.a(a[3]), .b(b[3]), .c(fulladder_2_carry), .Carry(fulladder_3_carry), .Sum(out[3]));
  FullAdder fulladder_4 (.a(a[4]), .b(b[4]), .c(fulladder_3_carry), .Carry(fulladder_4_carry), .Sum(out[4]));
  FullAdder fulladder_5 (.a(a[5]), .b(b[5]), .c(fulladder_4_carry), .Carry(fulladder_5_carry), .Sum(out[5]));
  FullAdder fulladder_6 (.a(a[6]), .b(b[6]), .c(fulladder_5_carry), .Carry(fulladder_6_carry), .Sum(out[6]));
  FullAdder fulladder_7 (.a(a[7]), .b(b[7]), .c(fulladder_6_carry), .Carry(fulladder_7_carry), .Sum(out[7]));
  FullAdder fulladder_8 (.a(a[8]), .b(b[8]), .c(fulladder_7_carry), .Carry(fulladder_8_carry), .Sum(out[8]));
  FullAdder fulladder_9 (.a(a[9]), .b(b[9]), .c(fulladder_8_carry), .Carry(fulladder_9_carry), .Sum(out[9]));
  FullAdder fulladder_10 (.a(a[10]), .b(b[10]), .c(fulladder_9_carry), .Carry(fulladder_10_carry), .Sum(out[10]));
  FullAdder fulladder_11 (.a(a[11]), .b(b[11]), .c(fulladder_10_carry), .Carry(fulladder_11_carry), .Sum(out[11]));
  FullAdder fulladder_12 (.a(a[12]), .b(b[12]), .c(fulladder_11_carry), .Carry(fulladder_12_carry), .Sum(out[12]));
  FullAdder fulladder_13 (.a(a[13]), .b(b[13]), .c(fulladder_12_carry), .Carry(fulladder_13_carry), .Sum(out[13]));
  FullAdder fulladder_14 (.a(a[14]), .b(b[14]), .c(fulladder_13_carry), .Carry(fulladder_14_carry), .Sum(out[14]));
  FullAdder fulladder_15 (.a(a[15]), .b(b[15]), .c(fulladder_14_carry), .Sum(out[15]));  // open: Carry
endmodule

module ALU (
  input  [15:0] x,
  input  zx,
  input  nx,
  input  [15:0] y,
  input  f,
  input  zy,
  input  ny,
  input  no,
  output [15:0] out,
  output ng,
  output zr
);

  wire [15:0] add16_1_out, and_1_out, and_2_out, and_3_out, mux4way16_1_out, mux4way16_2_out, mux16_2_out_4,
       not_1_out, not_2_out, not_3_out, not_4_out, not_5_out;

  assign not_1_out = ~x;  // NOT_Gate not_1, 16 bits wide
  assign not_2_out = ~y;  // NOT_Gate not_2, 16 bits wide
  assign and_1_out = not_1_out & x;  // AND_Gate and_1, 16 bits wide
  assign and_2_out = not_2_out & y;  // AND_Gate and_2, 16 bits wide
  Mux16 mux16_1 (.a(mux16_2_out_4), .b(not_5_out), .out_4({ng, out[14:0]}), .Sel(no));
  assign not_3_out = ~and_1_out;  // NOT_Gate not_3, 16 bits wide
  assign not_4_out = ~and_2_out;  // NOT_Gate not_4, 16 bits wide
  Mux4Way16 mux4way16_1 (.a(x), .b(not_1_out), .c(and_1_out), .d(not_3_out), .Out(mux4way16_1_out), .Sel({zx, nx}));
  assign and_3_out = mux4way16_1_out & mux4way16_2_out;  // AND_Gate and_3, 16 bits wide
  Mux4Way16 mux4way16_2 (.a(y), .b(not_2_out), .c(and_2_out), .d(not_4_out), .Out(mux4way16_2_out), .Sel({zy, ny}));
  Add16 add16_1 (.a(mux4way16_1_out), .b(mux4way16_2_out), .out(add16_1_out));
  Mux16 mux16_2 (.a(and_3_out), .b(add16_1_out), .out_4(mux16_2_out_4), .Sel(f));
  assign not_5_out = ~mux16_2_out_4;  // NOT_Gate not_5, 16 bits wide
  nor nor_1 (zr, out[0], out[1], out[2], out[3], out[4], out[5], out[6], out[7], out[8], out[9], out[10], out[11], out[12], out[13], out[14], ng);

  assign out[15] = ng;
endmodule

module PC (
  input  reset,
  input  [15:0] in,
  input  load,
  input  inc,
  input  Clock,
  output [15:0] out_6
);

  wire or_1_out, or_2_out;
  wire [15:0] and_1_out, inc16_1_out, mux4way16_1_out, mux16_1_out_4, not_1_out;

  assign not_1_out = ~in;  // NOT_Gate not_1, 16 bits wide
  assign and_1_out = not_1_out & in;  // AND_Gate and_1, 16 bits wide
  or or_1 (or_1_out, or_2_out, reset);
  Register #(.width(16)) register_1 (.D(mux16_1_out_4), .en(or_1_out), .Q(out_6), .clk(Clock));  // open: clr
  Inc16 inc16_1 (.in(out_6), .Out(inc16_1_out));
  Mux16 mux16_1 (.a(mux4way16_1_out), .b(and_1_out), .out_4(mux16_1_out_4), .Sel(reset));
  Mux4Way16 mux4way16_1 (.a(out_6), .b(inc16_1_out), .c(in), .d(in), .Out(mux4way16_1_out), .Sel({load, inc}));
  or or_2 (or_2_out, load, inc);
endmodule

module Inc16 (
  input  [15:0] in,
  output [15:0] Out
);

  wire halfadder_1_carry, halfadder_2_carry, halfadder_3_carry, halfadder_4_carry, halfadder_5_carry,
       halfadder_6_carry, halfadder_7_carry, halfadder_8_carry, halfadder_9_carry, halfadder_10_carry,
       halfadder_11_carry, halfadder_12_carry, halfadder_14_carry, halfadder_15_carry;

  HalfAdder halfadder_1 (.a(in[2]), .b(halfadder_2_carry), .Sum(Out[2]), .Carry(halfadder_1_carry));
  HalfAdder halfadder_2 (.a(in[1]), .b(in[0]), .Sum(Out[1]), .Carry(halfadder_2_carry));
  not not_1 (Out[0], in[0]);
  HalfAdder halfadder_3 (.a(in[4]), .b(halfadder_4_carry), .Sum(Out[4]), .Carry(halfadder_3_carry));
  HalfAdder halfadder_4 (.a(in[3]), .b(halfadder_1_carry), .Sum(Out[3]), .Carry(halfadder_4_carry));
  HalfAdder halfadder_5 (.a(in[7]), .b(halfadder_6_carry), .Sum(Out[7]), .Carry(halfadder_5_carry));
  HalfAdder halfadder_6 (.a(in[6]), .b(halfadder_7_carry), .Sum(Out[6]), .Carry(halfadder_6_carry));
  HalfAdder halfadder_7 (.a(in[5]), .b(halfadder_3_carry), .Sum(Out[5]), .Carry(halfadder_7_carry));
  HalfAdder halfadder_8 (.a(in[10]), .b(halfadder_9_carry), .Sum(Out[10]), .Carry(halfadder_8_carry));
  HalfAdder halfadder_9 (.a(in[9]), .b(halfadder_10_carry), .Sum(Out[9]), .Carry(halfadder_9_carry));
  HalfAdder halfadder_10 (.a(in[8]), .b(halfadder_5_carry), .Sum(Out[8]), .Carry(halfadder_10_carry));
  HalfAdder halfadder_11 (.a(in[12]), .b(halfadder_12_carry), .Sum(Out[12]), .Carry(halfadder_11_carry));
  HalfAdder halfadder_12 (.a(in[11]), .b(halfadder_8_carry), .Sum(Out[11]), .Carry(halfadder_12_carry));
  HalfAdder halfadder_13 (.a(in[15]), .b(halfadder_14_carry), .Sum(Out[15]));  // open: Carry
  HalfAdder halfadder_14 (.a(in[14]), .b(halfadder_15_carry), .Sum(Out[14]), .Carry(halfadder_14_carry));
  HalfAdder halfadder_15 (.a(in[13]), .b(halfadder_11_carry), .Sum(Out[13]), .Carry(halfadder_15_carry));
endmodule

module CPU (
  input  [15:0] inM,
  input  [15:0] instruction,
  input  Clock,
  input  reset,
  output [15:0] outM,
  output [14:0] pc,
  output [14:0] addressM,
  output writeM
);

  wire alu_1_ng, alu_1_zr, and_2_out, and_3_out, jge_out, jgt_out, jle_out, jmp_out, jne_out,
       multiplexer_1_out, not_1_out, not_2_out, null_out, or_1_out;
  wire [15:0] mux16_1_out_4, mux16_2_out_4, RegD_q;
  wire [15:15] pc_1_out_6, RegA_q;

  and and_1 (writeM, instruction[15], instruction[3]);
  and and_2 (and_2_out, instruction[4], instruction[15]);
  not not_1 (not_1_out, instruction[15]);
  Mux16 mux16_1 (.a(instruction), .b(outM), .out_4(mux16_1_out_4), .Sel(instruction[15]));
  Register #(.width(16)) RegD (.D(outM), .en(and_2_out), .Q(RegD_q), .clk(Clock));  // open: clr
  or or_1 (or_1_out, instruction[5], not_1_out);
  Register #(.width(16)) RegA (.D(mux16_1_out_4), .en(or_1_out), .Q({RegA_q[15], addressM}), .clk(Clock));  // open: clr
  Mux16 mux16_2 (.a(inM), .b({RegA_q[15], addressM}), .out_4(mux16_2_out_4), .Sel(instruction[12]));
  ALU alu_1 (
    .x(RegD_q), .zx(instruction[11]), .nx(instruction[10]), .y(mux16_2_out_4), .f(instruction[7]),
    .zy(instruction[9]), .ny(instruction[8]), .no(instruction[6]), .out(outM), .ng(alu_1_ng), .zr(alu_1_zr));
  or jmp (jmp_out, alu_1_ng, jge_out);
  and and_3 (and_3_out, multiplexer_1_out, instruction[15]);
  not not_2 (not_2_out, and_3_out);
  or jle (jle_out, alu_1_ng, alu_1_zr);
  or jne (jne_out, jgt_out, alu_1_ng);
  PC pc_1 (
    .reset(reset), .in({RegA_q[15], addressM}), .load(and_3_out), .inc(not_2_out),
    .out_6({pc_1_out_6[15], pc}), .Clock(Clock));
  nor jgt (jgt_out, alu_1_ng, alu_1_zr);
  and \null  (null_out, alu_1_ng, jgt_out);
  or jge (jge_out, alu_1_zr, jgt_out);
  Multiplexer #(.select(3), .enable("false")) multiplexer_1 (
    .in0(null_out), .in1(jgt_out), .in2(alu_1_zr), .in3(jge_out), .in4(alu_1_ng), .in5(jne_out),
    .in6(jle_out), .in7(jmp_out), .out(multiplexer_1_out), .sel(instruction[2:0]));
endmodule
